# Fritzing sketch compass (saved by Fritzing 0.9.3b)
breadboards: 1

parts:
  Часть1 = Arduino Pro Mini v13
  R1 = Resistor [tolerance=±5% resistance=220 package=THT]
  LED1 = LED - 5mm [color="Red (633nm)" package="5 mm [THT]"]
  Часть2 = Compass Module - HMC6352
  S1 = SWITCH-MOMENTARY-2 [package=tactile_switch_tall]
  SG1 = Buzzer 12mm [package=buzzer-12mm]

nets:
  N1: Часть1.A4, Часть2.SDA
  N2: Часть1.A5, Часть2.SCL
  GND: Часть1.GND, LED1.anode, Часть2.GND, S1.2, SG1.1
  N3: Часть1.D10_PWM/SS, Часть2.VCC
  N4: Часть1.D6_PWM, R1.Pin_1
  N5: Часть1.D5_PWM, SG1.2
  N6: Часть1.D2, S1.1
  N7: R1.Pin_0, LED1.cathode
